# Fritzing sketch sketch (saved by Fritzing 0.9.9b)

parts:
  U1 = LuaNode32 / ESP32 [part_number=ESP32S-PIN30]
  RY1 = SSR-40VA
  LED1 = LEDs [package=led10mm]

nets:
  N1: U1.D13, RY1.Pin_3
  N2: U1.GND, RY1.Pin_4
  N3: RY1.Pin_2, LED1.C

notes:
  230 V AC input

custom parts:
  LuaNode32 / ESP32: New Image for LuaNode32 DOIT ESP32 DEVKIT V1. Base parts from LuaNode32 / ESP32 ESP32 based LuaNode32 by G.Noorlander DOIT Esp32 DevKit v1 (30 pins long, 11 pins width) by Werner Rothschopf (modified by vanepp Dec 2018)
  SSR-40VA: SSR-40VA solid state relay.
  LEDs: LEDs Standard schematic elements and footprints for 5mm, 3mm, 1206, and 0603 sized LEDs. 5mm - Spark Fun Electronics SKU : COM-00529 (and others)
