# Fritzing sketch sketch (saved by Fritzing 0.9.9b)
circuit board: 6.3cm x 6.3cm
breadboards: 1

parts:
  U1 = LuaNode32 / ESP32 [part_number=ESP32S-PIN30]
  LED1 = smd LED [color="Red (633nm)" package="0805 [SMD]"]
  IC2 = ULN2803A [package=THT]
  LED2 = smd LED [color="Red (633nm)" package="0805 [SMD]"]
  LED3 = smd LED [color="Red (633nm)" package="0805 [SMD]"]
  R1 = Resistor [tolerance=±5% resistance=68 package=THT]
  R3 = Resistor [tolerance=±5% resistance=68 package=THT]
  R2 = Resistor [tolerance=±5% resistance=68 package=THT]

nets:
  N1: U1.D14, IC2.In_3
  N2: U1.D12, IC2.In_2
  N3: U1.D13, IC2.In_1
  N4: U1.GND, IC2.0V, R1.Pin_1, R3.Pin_1, R2.Pin_1
  N5: U1.Vin, IC2.COM_-_Common
  N6: LED1.cathode, R1.Pin_0
  N7: LED1.anode, IC2.Out_1
  N8: IC2.Out_3, LED3.anode
  N9: IC2.Out_2, LED2.anode
  N10: LED2.cathode, R2.Pin_0
  N11: LED3.cathode, R3.Pin_0

custom parts:
  LuaNode32 / ESP32: New Image for LuaNode32 DOIT ESP32 DEVKIT V1. Base parts from LuaNode32 / ESP32 ESP32 based LuaNode32 by G.Noorlander DOIT Esp32 DevKit v1 (30 pins long, 11 pins width) by Werner Rothschopf (modified by vanepp Dec 2018)
